// Digital circuit MainProcessor.dig as structural Verilog
module MainProcessor (
  input  [15:0] IN,
  input  clk,
  output [15:0] OUT
);

  wire ALUOp, ALUsrc, button_1_out, clk_t, DataSRC, dipswitch_1_out, MEM0, nclk, OUTen, PCsrc, PCsub,
       WriteData, writePTR;
  wire [2:0] OPcode;
  wire [12:0] ProgMem_d;
  wire [15:0] addsub_1_s, addsub_2_s, bitextender_1_out, multiplexer_1_out, multiplexer_3_out,
       multiplexer_4_out, PC_q, PTR_q, ramdualport_1_d;

  Register #(.Bits(16), .isProgramCounter("true")) PC (.D(addsub_1_s), .C(clk_t), .en(1'b1), .Q(PC_q));
  Multiplexer #(.Bits(16)) multiplexer_1 (.sel(PCsrc), .in_0(16'h1), .in_1(bitextender_1_out), .out(multiplexer_1_out));
  addsub addsub_1 (.A(PC_q), .B(multiplexer_1_out), .Sub(PCsub), .S(addsub_1_s));  // open: C_out
  ROM #(.AddrBits(16), .isProgramMemory("true"), .Bits(16)) ProgMem (.A(PC_q), .sel(1'b1), .D({OPcode, ProgMem_d}));
  Register #(.Bits(16)) PTR (.D(addsub_2_s), .C(clk_t), .en(writePTR), .Q(PTR_q));
  bitExtender bitextender_1 (.IN(ProgMem_d), .OUT(bitextender_1_out));
  ControlLogic controllogic_1 (
    .OP(OPcode), .MEM0(MEM0), .PCsrc(PCsrc), .PCsub(PCsub), .DataSRC(DataSRC), .OUTen(OUTen),
    .WritePTR(writePTR), .WriteData(WriteData), .ALUsrc(ALUsrc), .ALUOp(ALUOp));
  Button button_1 (.out(button_1_out));
  Multiplexer multiplexer_2 (.sel(dipswitch_1_out), .in_0(button_1_out), .in_1(clk), .out(clk_t));
  DipSwitch dipswitch_1 (.out(dipswitch_1_out));
  not not_1 (nclk, clk_t);
  Multiplexer #(.Bits(16)) multiplexer_3 (.sel(ALUsrc), .in_0(PTR_q), .in_1(ramdualport_1_d), .out(multiplexer_3_out));
  addsub addsub_2 (.A(multiplexer_3_out), .B(bitextender_1_out), .Sub(ALUOp), .S(addsub_2_s));  // open: C_out
  Multiplexer #(.Bits(16)) multiplexer_4 (.sel(DataSRC), .in_0(addsub_2_s), .in_1(IN), .out(multiplexer_4_out));
  RAMDualPort #(.AddrBits(16), .Bits(16)) ramdualport_1 (
    .A(PTR_q), .Din(multiplexer_4_out), .str(WriteData), .C(clk_t), .ld(1'b1), .D(ramdualport_1_d));
  Comparator #(.Bits(16)) comparator_1 (.a(ramdualport_1_d), .b({16{1'b0}}), .eq(MEM0));  // open: gt, lt
  Register #(.Bits(16)) OUTreg (.D(ramdualport_1_d), .C(clk_t), .en(OUTen), .Q(OUT));
  Terminal terminal_1 (.D(ramdualport_1_d), .C(clk_t), .en(OUTen));

  // Other names for the same wires on the sheet: sys_clk = clk

  // Notes on the sheet:
  //   IN: default 10
  //   clk: Hz: 100
  //   FetchStage
  //   contents of ProgMem (hex, n*v repeats v):
  //   a000,1,4001,1,4001,2002,c022,6001,2,c008,6001,1,4001,1,4001,2002
  //   ,e007,2001,c006,6001,2,4001,2002,e005,2,c006,6001,2001,4001,1
  //   ,e005,1,c006,6001,2003,4001,3,e005,2004,e021,2
  //   DecodeStage
  //   ExecuteStage
  //   MemoryStage
endmodule
