// Digital circuit addsub.dig as structural Verilog
module addsub (
  input  [15:0] A,
  input  [15:0] B,
  input  Sub,
  output [15:0] S,
  output C_out
);

  wire [15:0] bitextender_1_out, xor_1_out;

  BitExtender #(.inputBits(1)) bitextender_1 (.in(Sub), .out(bitextender_1_out));
  assign xor_1_out = B ^ bitextender_1_out;  // XOr xor_1, 16 bits wide
  Add #(.Bits(16)) add_1 (.a(A), .b(xor_1_out), .c_i(Sub), .s(S), .c_o(C_out));
endmodule
